# Fritzing sketch Led_feedback_shcmatic (saved by Fritzing 0.9.3b)
breadboards: 1

parts:
  Part1 = Arduino Uno (Rev3)
  LED2 = smd LED [color="Red (633nm)" package="0603 [SMD]"]
  LED3 = smd LED [color="Red (633nm)" package="0603 [SMD]"]
  LED4 = smd LED [color="Red (633nm)" package="0603 [SMD]"]
  LED5 = smd LED [color="Red (633nm)" package="0603 [SMD]"]
  R1 = Resistor [tolerance=±5% resistance=220 package="2512 [SMD]"]
  R2 = Resistor [tolerance=±5% resistance=220 package="0805 [SMD]"]
  R3 = Resistor [tolerance=±5% resistance=220 package="2010 [SMD]"]
  R4 = Resistor [tolerance=±5% resistance=220 package="2010 [SMD]"]

nets:
  N1: Part1.D9_PWM, LED2.anode
  N2: Part1.D2, LED5.anode
  N3: Part1.D3_PWM, LED4.anode
  N4: Part1.D6_PWM, LED3.anode
  N5: LED2.cathode, R1.Pin_0
  N6: LED3.cathode, R2.Pin_0
  N7: LED4.cathode, R3.Pin_0
  N8: LED5.cathode, R4.Pin_0
  N9: R1.Pin_1, R2.Pin_1, R3.Pin_1, R4.Pin_1

notes:
  220ohm resistors
