# Fritzing sketch midi_in_neoPixel_schematic (saved by Fritzing 0.9.3b)
breadboards: 1

parts:
  U4 = WS2812 RGB LED strip
  U5 = WS2812 RGB LED strip
  Pro_Micro6 = Pro Micro  # not connected
  S1 = Pushbutton [package="[THT]"]
  S2 = Pushbutton [package="[THT]"]
  S3 = Pushbutton [package="[THT]"]
  S4 = Pushbutton [package="[THT]"]
  S5 = Pushbutton [package="[THT]"]
  U6 = POT [package=alps_pot]

nets:
  N1: U4.GND, U5.GND#4
  N2: U4.VCC, U5.VCC#5
  N3: U4.DIN, U5.DOUT
  N4: U5.GND#0, S1.Pin_1, S1.Pin_2, S2.Pin_1, S2.Pin_2, S3.Pin_1, S3.Pin_2, S4.Pin_1, S4.Pin_2, S5.Pin_1, S5.Pin_2, U6.E
  N5: U5.VCC#1, U6.A
  N6: S1.Pin_3, S1.Pin_4
  N7: S2.Pin_3, S2.Pin_4
  N8: S3.Pin_3, S3.Pin_4
  N9: S4.Pin_3, S4.Pin_4
  N10: S5.Pin_3, S5.Pin_4

custom parts:
  WS2812 RGB LED strip: WS2812 strip
  Pro Micro: The SparkFun Pro Micro is a complete USB-based microcontoller development system, in a very small footprint, capable of implementing many types of projects. All programming can be done via the USB port.
