# Fritzing sketch CD4067 + Arduino_Uno_schematic (saved by Fritzing 0.9.1b)
breadboards: 1

parts:
  Part1 = Arduino Uno (Rev3) - ICSP
  HCF_1 = HCF 4067 [package="DIP24 [THT]"]
  U2 = POT [package=alps_pot]
  U3 = POT [package=alps_pot]
  U4 = POT [package=alps_pot]
  U5 = POT [package=alps_pot]
  U6 = POT [package=alps_pot]
  U7 = POT [package=alps_pot]

nets:
  N1: Part1.A0, HCF_1.1_O/I
  N2: Part1.5V, HCF_1.24_Vdd, U2.A, U3.A, U4.A, U5.A, U6.A, U7.A
  N3: Part1.GND, HCF_1.12_VSS, HCF_1.15_Inhibit, U2.E, U3.E, U4.E, U5.E, U6.E, U7.E
  N4: Part1.D2, HCF_1.10_A
  N5: Part1.D3_PWM, HCF_1.11_B
  N6: Part1.D4, HCF_1.14_C
  N7: Part1.D5_PWM, HCF_1.13_D
  N8: HCF_1.4_TG5, U7.S
  N9: HCF_1.5_TG4, U6.S
  N10: HCF_1.6_TG3, U5.S
  N11: HCF_1.7_TG2, U4.S
  N12: HCF_1.8_TG1, U3.S
  N13: HCF_1.9_TG0, U2.S
