# Fritzing sketch 1 - analog in out serial (saved by Fritzing 0.9.1b)
breadboards: 1

parts:
  Componente1 = Arduino Uno (Rev3)
  R1 = Rotary Potentiometer (Small) [maximum_resistance=5kΩ part_number=5k package=THT]
  LED1 = smd LED [color="Red (633nm)" package="1206 [SMD]"]
  R2 = Resistor [package="2512 [SMD]"]

nets:
  N1: Componente1.A0, R1.wiper
  N2: Componente1.D3_PWM, R2.Pin_1
  N3: Componente1.5V, R1.leg2
  N4: Componente1.GND, R1.leg1, LED1.cathode
  N5: LED1.anode, R2.Pin_0
