# Fritzing sketch prototype (saved by Fritzing 0.9.3b)
breadboards: 1

parts:
  Componente1 = Arduino Uno (Rev3)
  R3 = TRIMPOT [package=3362u-2]
  S2 = Pushbutton [package="[THT]"]
  S3 = Pushbutton [package="[THT]"]
  S4 = Pushbutton [package="[THT]"]
  R4 = TRIMPOT [package=3362u-2]

nets:
  N1: Componente1.A0, R3.WIPER
  N2: Componente1.A1, R4.WIPER
  N3: Componente1.D2, S2.Pin_3, S2.Pin_4
  N4: Componente1.D3_PWM, S3.Pin_3, S3.Pin_4
  N5: Componente1.D4, S4.Pin_3, S4.Pin_4
  N6: Componente1.5V, R3.CCW, R3.CW, R4.CW
  N7: Componente1.GND, S2.Pin_1, S2.Pin_2, S3.Pin_1, S3.Pin_2, S4.Pin_1, S4.Pin_2, R4.CCW
